// Logisim project project.circ as structural Verilog: 34 circuits, main circuit main
module main (
  input  [7:0] INPR,
  output [15:0] out_2,
  output [15:0] out_3,
  output [15:0] out_4,
  output [15:0] out_5,
  output [15:0] out_6,
  output [15:0] out_7,
  output [15:0] out_8,
  output [15:0] out_9
);

  wire ac_control_1_clr, ac_control_1_inc, ac_control_1_ld, ADD, AND, ar_control_1_clr, ar_control_1_inc,
       ar_control_1_ld, CLK, CLK_out, COMP, DR, dr_control_1_inc, dr_control_1_ld, E, E1, E2, E3, E4, E5, E6,
       E7, e_control_1_e_j, e_control_1_e_k, E_OUT, FGI, fgi_fgo_control_1_fgi_j, fgi_fgo_control_1_fgi_k,
       fgi_fgo_control_1_fgo_k, FGO, I, IEN, ien_control_1_ien_j, ien_control_1_ien_k, INPR_t,
       memory_control_1_ld, not_1_out, not_2_out, outr_control_1_ld, pc_control_1_clr, pc_control_1_inc,
       pc_control_1_ld, R, r_control_1_r_j, r_control_1_r_k, S, sc_control_1_clr, SHL, SHR, tr_control_1_ld;
  wire [7:0] D, outr_1_out;
  wire [11:0] B;
  wire [15:0] n16_bit_alu_1_alu_out, T;

  Hex_Digit_Display hex_digit_display_1 (.value(out_9[15:12]));  // open: dp
  Hex_Digit_Display hex_digit_display_2 (.value(out_9[7:4]));  // open: dp
  Hex_Digit_Display hex_digit_display_3 (.value(out_9[11:8]));  // open: dp
  Hex_Digit_Display hex_digit_display_4 (.value(out_9[3:0]));  // open: dp
  memory_control memory_control_1 (.T(T), .R(R), .D(D), .LD(memory_control_1_ld));
  AR ar_1 (
    .Bus_in(out_9), .CLK(CLK), .LD(ar_control_1_ld), .CLR(ar_control_1_clr), .INC(ar_control_1_inc),
    .Bus_out(out_3));
  PC pc_1 (
    .Bus_in(out_9), .CLK(CLK), .LD(pc_control_1_ld), .CLR(pc_control_1_clr), .INC(pc_control_1_inc),
    .Bus_out(out_4));
  DR dr_1 (.Bus_in(out_9), .LD(dr_control_1_ld), .Bus_out(out_5), .INC(dr_control_1_inc), .CLK(CLK));
  DR_control dr_control_1 (.T(T), .D(D), .LD(dr_control_1_ld), .INC(dr_control_1_inc));
  _16_bit_ALU u_16_bit_alu_1 (
    .DR(out_5), .AC(out_6), .INPR(INPR), .AND(AND), .ADD(ADD), .DR_2(DR), .INPR_2(INPR_t), .COM(COMP),
    .SHR(SHR), .SHL(SHL), .E(E), .ALU_out(n16_bit_alu_1_alu_out), .E_out(E_OUT));
  IR ir_1 (.R(R), .CLK(CLK), .I(I), .Buss_in(out_9), .Bus_out(out_7), .T(T), .D(D), .B(B));
  TR tr_1 (.Bus_in(out_9), .CLK(CLK), .LD(tr_control_1_ld), .Bus_out(out_8));
  TR_control tr_control_1 (.T(T), .R(R), .LD(tr_control_1_ld));
  OUTR_control outr_control_1 (.T(T), .D(D), .I(I), .B(B), .LD(outr_control_1_ld));
  RAM #(.addrWidth(12), .dataWidth(16), .bus("separate")) ram_1 (
    .addr(out_3[11:0]), .din(out_9), .data(out_2), .str(memory_control_1_ld), .clk(CLK), .ld(not_1_out));  // open: sel, clr
  not not_1 (not_1_out, memory_control_1_ld);
  OUTR outr_1 (.CLK(CLK), .LD(outr_control_1_ld), .Buss_in(out_9), .OUT(outr_1_out));
  AR_control ar_control_1 (
    .T(T), .I(I), .D(D), .R(R), .CLR(ar_control_1_clr), .LD(ar_control_1_ld), .INC(ar_control_1_inc));
  PC_control pc_control_1 (
    .T(T), .AC_16(out_6), .R(R), .DR_16(out_5), .D(D), .I(I), .B(B), .E(E), .FGO(FGO), .LD(pc_control_1_ld),
    .CLR(pc_control_1_clr), .INC(pc_control_1_inc), .FGI(FGI));
  AC ac_1 (
    .Bus_in(n16_bit_alu_1_alu_out), .CLK(CLK), .LD(ac_control_1_ld), .CLR(ac_control_1_clr),
    .INC(ac_control_1_inc), .Bus_out(out_6));
  AC_control ac_control_1 (
    .T(T), .I(I), .D(D), .B(B), .LD(ac_control_1_ld), .COMP(COMP), .SHR(SHR), .SHL(SHL),
    .CLR(ac_control_1_clr), .INC(ac_control_1_inc), .AND(AND), .ADD(ADD), .DR(DR), .INPR(INPR_t));
  Hex_Digit_Display hex_digit_display_5 (.value(out_4[15:12]));  // open: dp
  Hex_Digit_Display hex_digit_display_6 (.value(out_2[15:12]));  // open: dp
  Hex_Digit_Display hex_digit_display_7 (.value(out_2[11:8]));  // open: dp
  Hex_Digit_Display hex_digit_display_8 (.value(out_3[15:12]));  // open: dp
  Hex_Digit_Display hex_digit_display_9 (.value(out_3[11:8]));  // open: dp
  Hex_Digit_Display hex_digit_display_10 (.value(out_4[11:8]));  // open: dp
  Hex_Digit_Display hex_digit_display_11 (.value(out_5[11:8]));  // open: dp
  Hex_Digit_Display hex_digit_display_12 (.value(out_5[15:12]));  // open: dp
  Hex_Digit_Display hex_digit_display_13 (.value(out_6[11:8]));  // open: dp
  Hex_Digit_Display hex_digit_display_14 (.value(out_6[15:12]));  // open: dp
  Hex_Digit_Display hex_digit_display_15 (.value(out_7[15:12]));  // open: dp
  Hex_Digit_Display hex_digit_display_16 (.value(out_7[11:8]));  // open: dp
  Hex_Digit_Display hex_digit_display_17 (.value(out_8[11:8]));  // open: dp
  Hex_Digit_Display hex_digit_display_18 (.value(out_8[15:12]));  // open: dp
  Hex_Digit_Display hex_digit_display_19 (.value(outr_1_out[7:4]));  // open: dp
  Hex_Digit_Display hex_digit_display_20 (.value(out_2[3:0]));  // open: dp
  Hex_Digit_Display hex_digit_display_21 (.value(out_2[7:4]));  // open: dp
  Hex_Digit_Display hex_digit_display_22 (.value(out_3[7:4]));  // open: dp
  Hex_Digit_Display hex_digit_display_23 (.value(out_4[3:0]));  // open: dp
  Hex_Digit_Display hex_digit_display_24 (.value(out_4[7:4]));  // open: dp
  Hex_Digit_Display hex_digit_display_25 (.value(out_5[7:4]));  // open: dp
  Hex_Digit_Display hex_digit_display_26 (.value(out_5[3:0]));  // open: dp
  Hex_Digit_Display hex_digit_display_27 (.value(out_6[3:0]));  // open: dp
  Hex_Digit_Display hex_digit_display_28 (.value(out_6[7:4]));  // open: dp
  Hex_Digit_Display hex_digit_display_29 (.value(out_7[7:4]));  // open: dp
  Hex_Digit_Display hex_digit_display_30 (.value(out_8[3:0]));  // open: dp
  Hex_Digit_Display hex_digit_display_31 (.value(out_8[7:4]));  // open: dp
  Hex_Digit_Display hex_digit_display_32 (.value(outr_1_out[3:0]));  // open: dp
  assign out_9 = E7 ? out_2 : 16'bz;  // Controlled_Buffer controlled_buffer_1
  Hex_Digit_Display hex_digit_display_33 (.value(out_3[3:0]));  // open: dp
  assign out_9 = E1 ? out_3 : 16'bz;  // Controlled_Buffer controlled_buffer_2
  assign out_9 = E2 ? out_4 : 16'bz;  // Controlled_Buffer controlled_buffer_3
  assign out_9 = E3 ? out_5 : 16'bz;  // Controlled_Buffer controlled_buffer_4
  assign out_9 = E4 ? out_6 : 16'bz;  // Controlled_Buffer controlled_buffer_5
  Hex_Digit_Display hex_digit_display_34 (.value(out_7[3:0]));  // open: dp
  assign out_9 = E5 ? out_7 : 16'bz;  // Controlled_Buffer controlled_buffer_6
  assign out_9 = E6 ? out_8 : 16'bz;  // Controlled_Buffer controlled_buffer_7
  S s_1 (.T(T), .CLK(CLK), .I(I), .D(D), .B(B), .S(S));
  E_control e_control_1 (.T(T), .I(I), .D(D), .B(B), .E_j(e_control_1_e_j), .E_k(e_control_1_e_k), .E_out(E_OUT));
  SC_control sc_control_1 (.T(T), .R(R), .D(D), .I(I), .CLR(sc_control_1_clr));
  E e_1 (.E_k(e_control_1_e_k), .E_j(e_control_1_e_j), .CLK(CLK), .E(E));
  SC sc_1 (.CLR(sc_control_1_clr), .out_3(T), .CLK(CLK));
  FGI fgi_1 (.FGI_J(fgi_fgo_control_1_fgi_j), .CLK(CLK), .FGI_K(fgi_fgo_control_1_fgi_k), .FGI(FGI));
  FGI_FGO_control fgi_fgo_control_1 (
    .T(T), .I(I), .D(D), .B(B), .INPR(INPR), .FGI_K(fgi_fgo_control_1_fgi_k),
    .FGO_K(fgi_fgo_control_1_fgo_k), .FGI_J(fgi_fgo_control_1_fgi_j));
  Clock u_CLK (.out(CLK_out));
  not not_2 (not_2_out, S);
  FGO fgo_1 (.CLK(CLK), .FGO(FGO), .FGO_K(fgi_fgo_control_1_fgo_k));
  and and_1 (CLK, CLK_out, not_2_out);
  R_control r_control_1 (.T(T), .IEN(IEN), .FGI(FGI), .FGO(FGO), .R(R), .R_J(r_control_1_r_j), .R_K(r_control_1_r_k));
  IEN_control ien_control_1 (
    .T(T), .I(I), .D(D), .R(R), .B(B), .IEN_J(ien_control_1_ien_j), .IEN_K(ien_control_1_ien_k));
  R r_1 (.R_J(r_control_1_r_j), .CLK(CLK), .R_K(r_control_1_r_k), .R(R));
  IEN ien_1 (.IEN_J(ien_control_1_ien_j), .IEN_K(ien_control_1_ien_k), .IEN(IEN), .CLK(CLK));
  bus_selector bus_selector_1 (
    .T(T), .R(R), .D(D), .I(I), .B(B), .E1(E1), .E2(E2), .E3(E3), .E4(E4), .E5(E5), .E6(E6), .E7(E7));

  // Other names for the same wires on the sheet: AC_16[15:0] = out_6; DR_16[15:0] = out_5; INPR_8[7:0] = INPR
endmodule

module FA (
  input  Ai,
  input  Bi,
  input  Ci,
  output Di,
  output Ci_1
);

  wire and_1_out, and_2_out, xor_1_out;

  xor xor_1 (xor_1_out, Ai, Bi);
  and and_1 (and_1_out, Bi, Ai);
  xor xor_2 (Di, xor_1_out, Ci);
  and and_2 (and_2_out, xor_1_out, Ci);
  or or_1 (Ci_1, and_2_out, and_1_out);
endmodule

module logic_circuit (
  input  Bi,
  input  Ai,
  input  [1:0] S0,
  output Ei
);

  wire and_1_out, not_1_out, or_1_out, xor_1_out;

  and and_1 (and_1_out, Ai, Bi);
  or or_1 (or_1_out, Ai, Bi);
  xor xor_1 (xor_1_out, Ai, Bi);
  not not_1 (not_1_out, Ai);
  Multiplexer #(.select(2), .enable("false")) multiplexer_1 (
    .in0(and_1_out), .in1(or_1_out), .in2(xor_1_out), .in3(not_1_out), .out(Ei), .sel(S0));
endmodule

module IR (
  input  [15:0] T,
  input  [15:0] Buss_in,
  input  R,
  input  CLK,
  output [11:0] B,
  output I,
  output [15:0] Bus_out,
  output [7:0] D
);

  wire and_1_out, and_2_out, not_1_out;

  not not_1 (not_1_out, R);
  and and_1 (and_1_out, not_1_out, T[1]);
  and and_2 (and_2_out, not_1_out, T[2]);
  Register #(.width(16)) IR (.D(Buss_in), .en(and_1_out), .Q({Bus_out[15:12], B}), .clk(CLK));  // open: clr
  D_Flip_Flop u_I (.clk(CLK), .D(Bus_out[15]), .Q(I), .en(and_2_out));  // open: Qn, preset, reset
  Decoder #(.select(3), .enable("false")) decoder_1 (
    .out0(D[0]), .out1(D[1]), .out2(D[2]), .out3(D[3]), .out4(D[4]), .out5(D[5]), .out6(D[6]), .out7(D[7]),
    .sel(Bus_out[14:12]));

  assign Bus_out[11:0] = B;
endmodule

module AR (
  input  [15:0] Bus_in,
  input  CLK,
  input  LD,
  input  CLR,
  input  INC,
  output [15:0] Bus_out
);

  Counter #(.width(12), .max('hfff)) AR (
    .load(LD), .D(Bus_in[11:0]), .count(INC), .Q(Bus_out[11:0]), .clk(CLK), .clr(CLR));  // open: carry

  assign Bus_out[15:12] = 4'b0000;

  // Notes on the sheet:
  //   AR
endmodule

module PC (
  input  [15:0] Bus_in,
  input  CLK,
  input  LD,
  input  CLR,
  input  INC,
  output [15:0] Bus_out
);

  Counter #(.width(12), .max('hfff)) counter_1 (
    .load(LD), .D(Bus_in[11:0]), .count(INC), .Q(Bus_out[11:0]), .clk(CLK), .clr(CLR));  // open: carry

  assign Bus_out[15:12] = 4'b0000;

  // Notes on the sheet:
  //   PC
endmodule

module DR (
  input  [15:0] Bus_in,
  input  CLK,
  input  LD,
  input  INC,
  output [15:0] Bus_out
);

  Counter #(.width(16), .max('hffff)) counter_1 (
    .load(LD), .D(Bus_in), .count(INC), .Q(Bus_out), .clk(CLK));  // open: carry, clr

  // Notes on the sheet:
  //   DR
endmodule

module AC (
  input  [15:0] Bus_in,
  input  CLK,
  input  LD,
  input  CLR,
  input  INC,
  output [15:0] Bus_out
);

  Counter #(.width(16), .max('hffff)) counter_1 (
    .load(LD), .D(Bus_in), .count(INC), .Q(Bus_out), .clk(CLK), .clr(CLR));  // open: carry

  // Notes on the sheet:
  //   AC
endmodule

module TR (
  input  [15:0] Bus_in,
  input  CLK,
  input  LD,
  output [15:0] Bus_out
);

  Counter #(.width(16), .max('hffff)) counter_1 (
    .load(LD), .D(Bus_in), .count(1'b0), .Q(Bus_out), .clk(CLK));  // open: carry, clr

  // Notes on the sheet:
  //   TR
endmodule

module OUTR (
  input  [15:0] Buss_in,
  input  CLK,
  input  LD,
  output [7:0] OUT
);

  Register OUTR (.D(Buss_in[7:0]), .en(LD), .Q(OUT), .clk(CLK));  // open: clr
endmodule

module SC (
  input  CLR,
  input  CLK,
  output [15:0] out_3
);

  wire not_1_out;
  wire [3:0] counter_1_q;

  not not_1 (not_1_out, CLR);
  Counter #(.width(4), .max('hf)) counter_1 (
    .load(CLR), .D(4'b0000), .count(not_1_out), .Q(counter_1_q), .clk(CLK));  // open: carry, clr
  Decoder #(.select(4), .enable("false")) decoder_1 (
    .out0(out_3[0]), .out1(out_3[1]), .out2(out_3[2]), .out3(out_3[3]), .out4(out_3[4]), .out5(out_3[5]),
    .out6(out_3[6]), .out7(out_3[7]), .out8(out_3[8]), .out9(out_3[9]), .out10(out_3[10]), .out11(out_3[11]),
    .out12(out_3[12]), .out13(out_3[13]), .out14(out_3[14]), .out15(out_3[15]), .sel(counter_1_q));

  // Notes on the sheet:
  //   SC
endmodule

module S (
  input  [15:0] T,
  input  CLK,
  input  I,
  input  [7:0] D,
  input  [11:0] B,
  output S
);

  wire and_1_out, not_1_out, r_out;

  not not_1 (not_1_out, I);
  and r (r_out, D[7], not_1_out, T[3]);
  and and_1 (and_1_out, r_out, B[0]);
  J_K_Flip_Flop u_S (.J(and_1_out), .clk(CLK), .K(1'b0), .Q(S));  // open: Qn, preset, en, reset
endmodule

module E (
  input  E_j,
  input  CLK,
  input  E_k,
  output E
);

  J_K_Flip_Flop u_E (.J(E_j), .clk(CLK), .K(E_k), .Q(E));  // open: Qn, preset, en, reset
endmodule

module R (
  input  R_J,
  input  CLK,
  input  R_K,
  output R
);

  J_K_Flip_Flop u_R (.J(R_J), .clk(CLK), .K(R_K), .Q(R));  // open: Qn, preset, en, reset
endmodule

module FGI (
  input  FGI_J,
  input  CLK,
  input  FGI_K,
  output FGI
);

  J_K_Flip_Flop u_FGI (.J(FGI_J), .clk(CLK), .K(FGI_K), .Q(FGI));  // open: Qn, preset, en, reset
endmodule

module FGO (
  input  CLK,
  input  FGO_K,
  output FGO
);

  J_K_Flip_Flop u_FGO (.J(1'b0), .clk(CLK), .K(FGO_K), .Q(FGO));  // open: Qn, preset, en, reset
endmodule

module AR_control (
  input  [15:0] T,
  input  I,
  input  [7:0] D,
  input  R,
  output LD,
  output INC,
  output CLR
);

  wire and_1_out, and_2_out, and_3_out, not_1_out, not_2_out;

  not not_1 (not_1_out, D[7]);
  not not_2 (not_2_out, R);
  and and_1 (and_1_out, T[0], not_2_out);
  and and_2 (and_2_out, T[2], not_2_out);
  and and_3 (and_3_out, not_1_out, I, T[3]);
  and and_4 (CLR, R, T[0]);
  and and_5 (INC, D[5], T[4]);
  or or_1 (LD, and_3_out, and_1_out, and_2_out);
endmodule

module PC_control (
  input  [15:0] T,
  input  [15:0] AC_16,
  input  R,
  input  [15:0] DR_16,
  input  [7:0] D,
  input  I,
  input  [11:0] B,
  input  E,
  input  FGI,
  input  FGO,
  output LD,
  output CLR,
  output INC
);

  wire AC_all, and_1_out, and_2_out, and_4_out, and_5_out, and_6_out, and_7_out, and_8_out, and_9_out,
       and_10_out, and_11_out, and_12_out, and_13_out, and_14_out, DR_all, not_1_out, not_2_out, not_3_out,
       not_4_out, not_5_out, not_6_out;

  not not_1 (not_1_out, DR_all);
  and and_1 (and_1_out, D[5], T[5]);
  and and_2 (and_2_out, D[4], T[4]);
  not not_2 (not_2_out, R);
  not not_3 (not_3_out, I);
  or or_1 (LD, and_1_out, and_2_out);
  and and_3 (CLR, R, T[1]);
  and and_4 (and_4_out, not_3_out, D[7], T[3]);
  not not_4 (not_4_out, E);
  and and_5 (and_5_out, not_2_out, T[1]);
  and and_6 (and_6_out, R, T[2]);
  and and_7 (and_7_out, D[6], not_1_out, T[6]);
  not not_5 (not_5_out, AC_16[15]);
  and and_8 (and_8_out, not_4_out, and_4_out, B[1]);
  and and_9 (and_9_out, and_4_out, not_5_out, B[4]);
  and and_10 (and_10_out, AC_16[15], and_4_out, B[3]);
  not not_6 (not_6_out, AC_all);
  and and_11 (and_11_out, and_4_out, B[2], not_6_out);
  and and_12 (and_12_out, T[3], D[7], I);
  and and_13 (and_13_out, FGI, and_12_out, B[9]);
  and and_14 (and_14_out, and_12_out, FGO, B[8]);
  or or_2 (AC_all, AC_16[0], AC_16[1], AC_16[2], AC_16[3], AC_16[4], AC_16[5], AC_16[6], AC_16[7], AC_16[8], AC_16[9], AC_16[10], AC_16[11], AC_16[12], AC_16[13], AC_16[14], AC_16[15]);
  or or_3 (DR_all, DR_16[0], DR_16[1], DR_16[2], DR_16[3], DR_16[4], DR_16[5], DR_16[6], DR_16[7], DR_16[8], DR_16[9], DR_16[10], DR_16[11], DR_16[12], DR_16[13], DR_16[14], DR_16[15]);
  or or_4 (INC, and_5_out, and_6_out, and_7_out, and_9_out, and_10_out, and_11_out, and_8_out, and_13_out, and_14_out);

  // Other names for the same wires on the sheet: AC15 = AC_16[15]

  // Notes on the sheet:
  //   r
  //   P
endmodule

module DR_control (
  input  [15:0] T,
  input  [7:0] D,
  output LD,
  output INC
);

  wire and_1_out, and_3_out, and_4_out, and_5_out;

  and and_1 (and_1_out, T[4], D[6]);
  and and_2 (INC, T[5], D[6]);
  and and_3 (and_3_out, T[4], D[0]);
  and and_4 (and_4_out, T[4], D[1]);
  and and_5 (and_5_out, T[4], D[2]);
  or or_1 (LD, and_3_out, and_4_out, and_5_out, and_1_out);
endmodule

module AC_control (
  input  [15:0] T,
  input  I,
  input  [7:0] D,
  input  [11:0] B,
  output AND,
  output ADD,
  output DR,
  output LD,
  output COMP,
  output SHR,
  output SHL,
  output INPR,
  output CLR,
  output INC
);

  wire not_1_out, P, r;

  not not_1 (not_1_out, I);
  and and_1 (SHL, r, B[6]);
  and and_2 (AND, T[5], D[0]);
  and and_3 (ADD, T[5], D[1]);
  and and_4 (DR, T[5], D[2]);
  and u_r (r, D[7], not_1_out, T[3]);
  and u_P (P, D[7], I, T[3]);
  and and_5 (COMP, r, B[9]);
  and and_6 (SHR, r, B[7]);
  and and_7 (INPR, B[11], P);
  and and_8 (CLR, B[11], r);
  and and_9 (INC, B[5], r);
  or or_1 (LD, AND, ADD, DR, COMP, SHR, SHL, INPR);
endmodule

module TR_control (
  input  [15:0] T,
  input  R,
  output LD
);

  and and_1 (LD, R, T[0]);
endmodule

module OUTR_control (
  input  [15:0] T,
  input  [7:0] D,
  input  I,
  input  [11:0] B,
  output LD
);

  wire P;

  and and_1 (LD, B[10], P);
  and u_P (P, D[7], I, T[3]);
endmodule

module SC_control (
  input  [15:0] T,
  input  R,
  input  [7:0] D,
  input  I,
  output CLR
);

  wire and_1_out, and_2_out, and_3_out, and_4_out, and_5_out, and_6_out, and_7_out, and_8_out, not_1_out,
       p_out, r_out;

  not not_1 (not_1_out, I);
  and and_1 (and_1_out, R, T[2]);
  and and_2 (and_2_out, T[5], D[0]);
  and and_3 (and_3_out, T[5], D[1]);
  and and_4 (and_4_out, T[5], D[2]);
  and and_5 (and_5_out, T[5], D[5]);
  and and_6 (and_6_out, T[4], D[3]);
  and and_7 (and_7_out, T[4], D[4]);
  and and_8 (and_8_out, T[6], D[6]);
  and u_r (r_out, D[7], not_1_out, T[3]);
  and p (p_out, D[7], I, T[3]);
  or or_1 (CLR, and_1_out, and_2_out, and_3_out, and_4_out, and_5_out, and_6_out, and_7_out, and_8_out, r_out, p_out);
endmodule

module IEN_control (
  input  [15:0] T,
  input  I,
  input  [7:0] D,
  input  R,
  input  [11:0] B,
  output IEN_J,
  output IEN_K
);

  wire and_2_out, and_3_out, P;

  and u_P (P, D[7], I, T[3]);
  and and_1 (IEN_J, B[7], P);
  and and_2 (and_2_out, P, B[6]);
  and and_3 (and_3_out, R, T[2]);
  or or_1 (IEN_K, and_2_out, and_3_out);
endmodule

module FGI_FGO_control (
  input  [15:0] T,
  input  I,
  input  [7:0] D,
  input  [11:0] B,
  input  [7:0] INPR,
  output FGI_K,
  output FGO_K,
  output FGI_J
);

  wire P_out;

  and P (P_out, D[7], I, T[3]);
  and and_1 (FGI_K, P_out, B[11]);
  and and_2 (FGO_K, P_out, B[10]);
  or or_1 (FGI_J, INPR[0], INPR[1], INPR[2], INPR[3], INPR[4], INPR[5], INPR[6], INPR[7]);
endmodule

module E_control (
  input  [15:0] T,
  input  I,
  input  [7:0] D,
  input  [11:0] B,
  input  E_out,
  output E_j,
  output E_k
);

  wire and_1_out, and_2_out, and_3_out, and_4_out, not_1_out, not_2_out, not_3_out, or_1_out, r;

  and and_1 (and_1_out, r, B[10]);
  and and_2 (and_2_out, r, B[8]);
  or or_1 (or_1_out, and_2_out, and_1_out);
  not not_1 (not_1_out, or_1_out);
  not not_2 (not_2_out, I);
  not not_3 (not_3_out, E_out);
  and u_r (r, D[7], not_2_out, T[3]);
  and and_3 (and_3_out, E_out, not_1_out);
  and and_4 (and_4_out, not_3_out, not_1_out);
  or or_2 (E_j, and_2_out, and_3_out);
  or or_3 (E_k, and_4_out, and_2_out, and_1_out);
endmodule

module R_control (
  input  [15:0] T,
  input  IEN,
  input  FGI,
  input  FGO,
  input  R,
  output R_J,
  output R_K
);

  wire not_1_out, not_2_out, not_3_out, or_1_out;

  not not_1 (not_1_out, T[0]);
  not not_2 (not_2_out, T[1]);
  or or_1 (or_1_out, FGI, FGO);
  not not_3 (not_3_out, T[2]);
  and and_1 (R_K, T[2], R);
  and and_2 (R_J, not_1_out, not_2_out, IEN, or_1_out, not_3_out);
endmodule

module _16_bit_adder (
  input  A0,
  input  A14,
  input  B0,
  input  B14,
  input  A14_2,
  input  A1,
  input  B14_2,
  input  B1,
  input  A13,
  input  A2,
  input  B13,
  input  B2,
  input  A3,
  input  A12,
  input  B3,
  input  B12,
  input  A11,
  input  A4,
  input  B11,
  input  B4,
  input  A10,
  input  A5,
  input  B10,
  input  B5,
  input  A6,
  input  A9,
  input  B6,
  input  B9,
  input  A7,
  input  A8,
  input  B7,
  input  B8,
  output S15,
  output S0,
  output CARRY,
  output S14,
  output S1,
  output S2,
  output S13,
  output S3,
  output S12,
  output S4,
  output S11,
  output S5,
  output S10,
  output S6,
  output S9,
  output S7,
  output S8
);

  wire fa_1_ci_1, fa_2_ci_1, fa_3_ci_1, fa_4_ci_1, fa_5_ci_1, fa_6_ci_1, fa_7_ci_1, fa_8_ci_1, fa_10_ci_1,
       fa_11_ci_1, fa_12_ci_1, fa_13_ci_1, fa_14_ci_1, fa_15_ci_1, fa_16_ci_1;

  FA fa_1 (.Ai(A0), .Bi(B0), .Ci(1'b0), .Di(S0), .Ci_1(fa_1_ci_1));
  FA fa_2 (.Ai(A1), .Bi(B1), .Ci(fa_1_ci_1), .Di(S1), .Ci_1(fa_2_ci_1));
  FA fa_3 (.Ai(A2), .Bi(B2), .Ci(fa_2_ci_1), .Di(S2), .Ci_1(fa_3_ci_1));
  FA fa_4 (.Ai(A3), .Bi(B3), .Ci(fa_3_ci_1), .Di(S3), .Ci_1(fa_4_ci_1));
  FA fa_5 (.Ai(A4), .Bi(B4), .Ci(fa_4_ci_1), .Di(S4), .Ci_1(fa_5_ci_1));
  FA fa_6 (.Ai(A5), .Bi(B5), .Ci(fa_5_ci_1), .Di(S5), .Ci_1(fa_6_ci_1));
  FA fa_7 (.Ai(A6), .Bi(B6), .Ci(fa_6_ci_1), .Di(S6), .Ci_1(fa_7_ci_1));
  FA fa_8 (.Ai(A7), .Bi(B7), .Ci(fa_7_ci_1), .Di(S7), .Ci_1(fa_8_ci_1));
  FA fa_9 (.Ai(A14), .Bi(B14), .Ci(fa_10_ci_1), .Di(S15), .Ci_1(CARRY));
  FA fa_10 (.Ai(A14_2), .Bi(B14_2), .Ci(fa_11_ci_1), .Di(S14), .Ci_1(fa_10_ci_1));
  FA fa_11 (.Ai(A13), .Bi(B13), .Ci(fa_12_ci_1), .Di(S13), .Ci_1(fa_11_ci_1));
  FA fa_12 (.Ai(A12), .Bi(B12), .Ci(fa_13_ci_1), .Di(S12), .Ci_1(fa_12_ci_1));
  FA fa_13 (.Ai(A11), .Bi(B11), .Ci(fa_14_ci_1), .Di(S11), .Ci_1(fa_13_ci_1));
  FA fa_14 (.Ai(A10), .Bi(B10), .Ci(fa_15_ci_1), .Di(S10), .Ci_1(fa_14_ci_1));
  FA fa_15 (.Ai(A9), .Bi(B9), .Ci(fa_16_ci_1), .Di(S9), .Ci_1(fa_15_ci_1));
  FA fa_16 (.Ai(A8), .Bi(B8), .Ci(fa_8_ci_1), .Di(S8), .Ci_1(fa_16_ci_1));
endmodule

module _12_bit_adder (
  input  A0,
  input  A1,
  input  A2,
  input  A3,
  input  A4,
  input  A5,
  input  B0,
  input  B1,
  input  B2,
  input  B3,
  input  B4,
  input  B5,
  input  B11,
  input  B10,
  input  B9,
  input  B8,
  input  B7,
  input  B6,
  input  A11,
  input  A10,
  input  A9,
  input  A8,
  input  A7,
  input  A6,
  output S0,
  output S1,
  output S2,
  output S3,
  output S4,
  output S5,
  output CARRY,
  output S11,
  output S10,
  output S9,
  output S8,
  output S7,
  output S6
);

  wire fa_1_ci_1, fa_3_ci_1, fa_4_ci_1, fa_5_ci_1, fa_6_ci_1, fa_7_ci_1, fa_8_ci_1, fa_9_ci_1, fa_10_ci_1,
       fa_11_ci_1, fa_12_ci_1;

  FA fa_1 (.Ai(A0), .Bi(B0), .Ci(1'b0), .Di(S0), .Ci_1(fa_1_ci_1));
  FA fa_2 (.Ai(A11), .Bi(B11), .Ci(fa_3_ci_1), .Di(S11), .Ci_1(CARRY));
  FA fa_3 (.Ai(A10), .Bi(B10), .Ci(fa_5_ci_1), .Di(S10), .Ci_1(fa_3_ci_1));
  FA fa_4 (.Ai(A1), .Bi(B1), .Ci(fa_1_ci_1), .Di(S1), .Ci_1(fa_4_ci_1));
  FA fa_5 (.Ai(A9), .Bi(B9), .Ci(fa_7_ci_1), .Di(S9), .Ci_1(fa_5_ci_1));
  FA fa_6 (.Ai(A2), .Bi(B2), .Ci(fa_4_ci_1), .Di(S2), .Ci_1(fa_6_ci_1));
  FA fa_7 (.Ai(A8), .Bi(B8), .Ci(fa_9_ci_1), .Di(S8), .Ci_1(fa_7_ci_1));
  FA fa_8 (.Ai(A3), .Bi(B3), .Ci(fa_6_ci_1), .Di(S3), .Ci_1(fa_8_ci_1));
  FA fa_9 (.Ai(A7), .Bi(B7), .Ci(fa_12_ci_1), .Di(S7), .Ci_1(fa_9_ci_1));
  FA fa_10 (.Ai(A4), .Bi(B4), .Ci(fa_8_ci_1), .Di(S4), .Ci_1(fa_10_ci_1));
  FA fa_11 (.Ai(A5), .Bi(B5), .Ci(fa_10_ci_1), .Di(S5), .Ci_1(fa_11_ci_1));
  FA fa_12 (.Ai(A6), .Bi(B6), .Ci(fa_11_ci_1), .Di(S6), .Ci_1(fa_12_ci_1));
endmodule

module _1_bit_ALU (
  input  DR_i,
  input  C_i,
  input  INPR_i,
  input  AC_i,
  input  AND,
  input  ADD,
  input  DR,
  input  INPR,
  input  COM,
  input  SHR,
  input  AC_i_1,
  input  SHL,
  input  AC_i_1_2,
  output C_i_1,
  output ALU_OUT
);

  wire ADD_out, AND_out, COM_out, DR_out, fa_1_di, INPR_out, not_1_out, SHL_out, SHR_out;

  FA fa_1 (.Ai(AC_i), .Bi(DR_i), .Ci(C_i), .Di(fa_1_di), .Ci_1(C_i_1));
  not not_1 (not_1_out, AC_i);
  and u_AND (AND_out, DR_i, AC_i, AND);
  and u_ADD (ADD_out, ADD, fa_1_di);
  and u_DR (DR_out, DR_i, DR);
  and u_INPR (INPR_out, INPR_i, INPR);
  and u_COM (COM_out, not_1_out, COM);
  and u_SHR (SHR_out, SHR, AC_i_1);
  and u_SHL (SHL_out, SHL, AC_i_1_2);
  or or_1 (ALU_OUT, AND_out, ADD_out, DR_out, INPR_out, COM_out, SHR_out, SHL_out);

  // Other names for the same wires on the sheet: INP_i = INPR_i
endmodule

module _16_bit_ALU (
  input  [15:0] DR,
  input  [15:0] AC,
  input  [7:0] INPR,
  input  AND,
  input  ADD,
  input  DR_2,
  input  INPR_2,
  input  COM,
  input  SHR,
  input  SHL,
  input  E,
  output E_out,
  output [15:0] ALU_out
);

  wire and_1_out, and_2_out, and_3_out, and_4_out, last_cout, n1_bit_alu_1_c_i_1, n1_bit_alu_2_c_i_1,
       n1_bit_alu_3_c_i_1, n1_bit_alu_4_c_i_1, n1_bit_alu_5_c_i_1, n1_bit_alu_6_c_i_1, n1_bit_alu_7_c_i_1,
       n1_bit_alu_8_c_i_1, n1_bit_alu_9_c_i_1, n1_bit_alu_10_c_i_1, n1_bit_alu_11_c_i_1, n1_bit_alu_12_c_i_1,
       n1_bit_alu_13_c_i_1, n1_bit_alu_14_c_i_1, n1_bit_alu_15_c_i_1, not_1_out, not_2_out, not_3_out,
       or_1_out;

  _1_bit_ALU u_1_bit_alu_1 (
    .DR_i(DR[0]), .C_i(1'b0), .INPR_i(INPR[0]), .AC_i(AC[0]), .AND(AND), .ADD(ADD), .DR(DR_2), .INPR(INPR_2),
    .COM(COM), .SHR(SHR), .AC_i_1(AC[1]), .SHL(SHL), .AC_i_1_2(E), .C_i_1(n1_bit_alu_1_c_i_1),
    .ALU_OUT(ALU_out[0]));
  _1_bit_ALU u_1_bit_alu_2 (
    .DR_i(DR[2]), .C_i(n1_bit_alu_9_c_i_1), .INPR_i(INPR[2]), .AC_i(AC[2]), .AND(AND), .ADD(ADD), .DR(DR_2),
    .INPR(INPR_2), .COM(COM), .SHR(SHR), .AC_i_1(AC[3]), .SHL(SHL), .AC_i_1_2(AC[1]),
    .C_i_1(n1_bit_alu_2_c_i_1), .ALU_OUT(ALU_out[2]));
  _1_bit_ALU u_1_bit_alu_3 (
    .DR_i(DR[4]), .C_i(n1_bit_alu_10_c_i_1), .INPR_i(INPR[4]), .AC_i(AC[4]), .AND(AND), .ADD(ADD), .DR(DR_2),
    .INPR(INPR_2), .COM(COM), .SHR(SHR), .AC_i_1(AC[5]), .SHL(SHL), .AC_i_1_2(AC[3]),
    .C_i_1(n1_bit_alu_3_c_i_1), .ALU_OUT(ALU_out[4]));
  _1_bit_ALU u_1_bit_alu_4 (
    .DR_i(DR[6]), .C_i(n1_bit_alu_11_c_i_1), .INPR_i(INPR[6]), .AC_i(AC[6]), .AND(AND), .ADD(ADD), .DR(DR_2),
    .INPR(INPR_2), .COM(COM), .SHR(SHR), .AC_i_1(AC[7]), .SHL(SHL), .AC_i_1_2(AC[5]),
    .C_i_1(n1_bit_alu_4_c_i_1), .ALU_OUT(ALU_out[6]));
  _1_bit_ALU u_1_bit_alu_5 (
    .DR_i(DR[8]), .C_i(n1_bit_alu_12_c_i_1), .INPR_i(1'b0), .AC_i(AC[8]), .AND(AND), .ADD(ADD), .DR(DR_2),
    .INPR(INPR_2), .COM(COM), .SHR(SHR), .AC_i_1(AC[9]), .SHL(SHL), .AC_i_1_2(AC[7]),
    .C_i_1(n1_bit_alu_5_c_i_1), .ALU_OUT(ALU_out[8]));
  _1_bit_ALU u_1_bit_alu_6 (
    .DR_i(DR[10]), .C_i(n1_bit_alu_13_c_i_1), .INPR_i(1'b0), .AC_i(AC[10]), .AND(AND), .ADD(ADD), .DR(DR_2),
    .INPR(INPR_2), .COM(COM), .SHR(SHR), .AC_i_1(AC[11]), .SHL(SHL), .AC_i_1_2(AC[9]),
    .C_i_1(n1_bit_alu_6_c_i_1), .ALU_OUT(ALU_out[10]));
  _1_bit_ALU u_1_bit_alu_7 (
    .DR_i(DR[12]), .C_i(n1_bit_alu_14_c_i_1), .INPR_i(1'b0), .AC_i(AC[12]), .AND(AND), .ADD(ADD), .DR(DR_2),
    .INPR(INPR_2), .COM(COM), .SHR(SHR), .AC_i_1(AC[13]), .SHL(SHL), .AC_i_1_2(AC[11]),
    .C_i_1(n1_bit_alu_7_c_i_1), .ALU_OUT(ALU_out[12]));
  _1_bit_ALU u_1_bit_alu_8 (
    .DR_i(DR[14]), .C_i(n1_bit_alu_15_c_i_1), .INPR_i(1'b0), .AC_i(AC[14]), .AND(AND), .ADD(ADD), .DR(DR_2),
    .INPR(INPR_2), .COM(COM), .SHR(SHR), .AC_i_1(AC[15]), .SHL(SHL), .AC_i_1_2(AC[13]),
    .C_i_1(n1_bit_alu_8_c_i_1), .ALU_OUT(ALU_out[14]));
  _1_bit_ALU u_1_bit_alu_9 (
    .DR_i(DR[1]), .C_i(n1_bit_alu_1_c_i_1), .INPR_i(INPR[1]), .AC_i(AC[1]), .AND(AND), .ADD(ADD), .DR(DR_2),
    .INPR(INPR_2), .COM(COM), .SHR(SHR), .AC_i_1(AC[2]), .SHL(SHL), .AC_i_1_2(AC[0]),
    .C_i_1(n1_bit_alu_9_c_i_1), .ALU_OUT(ALU_out[1]));
  _1_bit_ALU u_1_bit_alu_10 (
    .DR_i(DR[3]), .C_i(n1_bit_alu_2_c_i_1), .INPR_i(INPR[3]), .AC_i(AC[3]), .AND(AND), .ADD(ADD), .DR(DR_2),
    .INPR(INPR_2), .COM(COM), .SHR(SHR), .AC_i_1(AC[4]), .SHL(SHL), .AC_i_1_2(AC[2]),
    .C_i_1(n1_bit_alu_10_c_i_1), .ALU_OUT(ALU_out[3]));
  _1_bit_ALU u_1_bit_alu_11 (
    .DR_i(DR[5]), .C_i(n1_bit_alu_3_c_i_1), .INPR_i(INPR[5]), .AC_i(AC[5]), .AND(AND), .ADD(ADD), .DR(DR_2),
    .INPR(INPR_2), .COM(COM), .SHR(SHR), .AC_i_1(AC[6]), .SHL(SHL), .AC_i_1_2(AC[4]),
    .C_i_1(n1_bit_alu_11_c_i_1), .ALU_OUT(ALU_out[5]));
  _1_bit_ALU u_1_bit_alu_12 (
    .DR_i(DR[7]), .C_i(n1_bit_alu_4_c_i_1), .INPR_i(INPR[7]), .AC_i(AC[7]), .AND(AND), .ADD(ADD), .DR(DR_2),
    .INPR(INPR_2), .COM(COM), .SHR(SHR), .AC_i_1(AC[8]), .SHL(SHL), .AC_i_1_2(AC[6]),
    .C_i_1(n1_bit_alu_12_c_i_1), .ALU_OUT(ALU_out[7]));
  _1_bit_ALU u_1_bit_alu_13 (
    .DR_i(DR[9]), .C_i(n1_bit_alu_5_c_i_1), .INPR_i(1'b0), .AC_i(AC[9]), .AND(AND), .ADD(ADD), .DR(DR_2),
    .INPR(INPR_2), .COM(COM), .SHR(SHR), .AC_i_1(AC[10]), .SHL(SHL), .AC_i_1_2(AC[8]),
    .C_i_1(n1_bit_alu_13_c_i_1), .ALU_OUT(ALU_out[9]));
  _1_bit_ALU u_1_bit_alu_14 (
    .DR_i(DR[11]), .C_i(n1_bit_alu_6_c_i_1), .INPR_i(1'b0), .AC_i(AC[11]), .AND(AND), .ADD(ADD), .DR(DR_2),
    .INPR(INPR_2), .COM(COM), .SHR(SHR), .AC_i_1(AC[12]), .SHL(SHL), .AC_i_1_2(AC[10]),
    .C_i_1(n1_bit_alu_14_c_i_1), .ALU_OUT(ALU_out[11]));
  _1_bit_ALU u_1_bit_alu_15 (
    .DR_i(DR[13]), .C_i(n1_bit_alu_7_c_i_1), .INPR_i(1'b0), .AC_i(AC[13]), .AND(AND), .ADD(ADD), .DR(DR_2),
    .INPR(INPR_2), .COM(COM), .SHR(SHR), .AC_i_1(AC[14]), .SHL(SHL), .AC_i_1_2(AC[12]),
    .C_i_1(n1_bit_alu_15_c_i_1), .ALU_OUT(ALU_out[13]));
  _1_bit_ALU u_1_bit_alu_16 (
    .DR_i(DR[15]), .C_i(n1_bit_alu_8_c_i_1), .INPR_i(1'b0), .AC_i(AC[15]), .AND(AND), .ADD(ADD), .DR(DR_2),
    .INPR(INPR_2), .COM(COM), .SHR(SHR), .AC_i_1(E), .SHL(SHL), .AC_i_1_2(AC[14]), .C_i_1(last_cout),
    .ALU_OUT(ALU_out[15]));
  and and_1 (and_1_out, AC[15], SHL);
  and and_2 (and_2_out, AC[0], SHR);
  and and_3 (and_3_out, last_cout, ADD);
  not not_1 (not_1_out, and_1_out);
  not not_2 (not_2_out, and_3_out);
  or or_1 (or_1_out, and_1_out, and_2_out, and_3_out);
  not not_3 (not_3_out, and_2_out);
  and and_4 (and_4_out, not_1_out, not_3_out, not_2_out, E);
  or or_2 (E_out, or_1_out, and_4_out);

  // Other names for the same wires on the sheet: AC_0 = AC[0]; AC_15 = AC[15]; ALU_0 = ALU_out[0]; ALU_1 = ALU_out[1];
  //   ALU_2 = ALU_out[2]; ALU_3 = ALU_out[3]; ALU_4 = ALU_out[4]; ALU_5 = ALU_out[5]; ALU_6 = ALU_out[6];
  //   ALU_7 = ALU_out[7]; ALU_8 = ALU_out[8]; ALU_9 = ALU_out[9]; ALU_10 = ALU_out[10]; ALU_11 = ALU_out[11];
  //   ALU_12 = ALU_out[12]; ALU_13 = ALU_out[13]; ALU_14 = ALU_out[14]; ALU_15 = ALU_out[15]; DR_t = DR_2; E_in = E;
  //   INP0 = INPR[0]; INP1 = INPR[1]; INP2 = INPR[2]; INP3 = INPR[3]; INP4 = INPR[4]; INP5 = INPR[5]; INP6 = INPR[6];
  //   INP7 = INPR[7]; INPR_t = INPR_2
endmodule

module memory_control (
  input  [15:0] T,
  input  R,
  input  [7:0] D,
  output LD
);

  wire and_1_out, and_2_out, and_3_out, and_4_out;

  and and_1 (and_1_out, R, T[1]);
  and and_2 (and_2_out, D[3], T[4]);
  and and_3 (and_3_out, T[4], D[5]);
  and and_4 (and_4_out, D[6], T[6]);
  or or_1 (LD, and_1_out, and_2_out, and_3_out, and_4_out);
endmodule

module IEN (
  input  CLK,
  input  IEN_J,
  input  IEN_K,
  output IEN
);

  J_K_Flip_Flop u_IEN (.J(IEN_J), .clk(CLK), .K(IEN_K), .Q(IEN));  // open: Qn, preset, en, reset
endmodule

module bus_selector (
  input  [15:0] T,
  input  R,
  input  [7:0] D,
  input  I,
  input  [11:0] B,
  output E1,
  output E2,
  output E3,
  output E4,
  output E5,
  output E6,
  output E7
);

  wire and_1_out, and_2_out, and_3_out, and_4_out, and_7_out, and_8_out, and_9_out, and_10_out, and_11_out,
       and_12_out, and_13_out, and_14_out, and_15_out, and_16_out, and_17_out, not_1_out, not_2_out,
       not_3_out, P_out;

  not not_1 (not_1_out, R);
  and and_1 (and_1_out, D[4], T[4]);
  and and_2 (and_2_out, D[5], T[5]);
  and and_3 (and_3_out, R, T[0]);
  not not_2 (not_2_out, R);
  and and_4 (and_4_out, D[3], T[4]);
  and P (P_out, D[7], I, T[3]);
  and and_5 (E5, T[2], not_1_out);
  and and_6 (E6, R, T[1]);
  or or_1 (E1, and_1_out, and_2_out);
  and and_7 (and_7_out, D[5], T[4]);
  and and_8 (and_8_out, not_2_out, T[0]);
  and and_9 (and_9_out, T[5], D[2]);
  and and_10 (and_10_out, D[6], T[6]);
  and and_11 (and_11_out, P_out, B[10]);
  or or_2 (E2, and_7_out, and_3_out, and_8_out);
  or or_3 (E3, and_9_out, and_10_out);
  or or_4 (E4, and_4_out, and_11_out);
  not not_3 (not_3_out, D[7]);
  and and_12 (and_12_out, not_3_out, I, T[3]);
  and and_13 (and_13_out, T[4], D[0]);
  and and_14 (and_14_out, T[4], D[1]);
  and and_15 (and_15_out, T[4], D[2]);
  and and_16 (and_16_out, T[4], D[6]);
  and and_17 (and_17_out, ~R, T[1]);  // AND_Gate
  or or_5 (E7, and_12_out, and_13_out, and_14_out, and_15_out, and_16_out, and_17_out);
endmodule
